// Logisim project AlarmCounter.circ as structural Verilog: 1 circuit, main circuit main
module main (
  input  in_1,
  input  in_2
);

  wire clock_1_out, d_ff_1_q, decoder_1_out0, decoder_1_out1, decoder_1_out2, decoder_1_out3,
       multiplexer_1_out, multiplexer_2_out, not_1_out, xor_1_out, xor_2_out;
  wire [1:0] counter_1_q;
  wire [3:0] bcd_to_7_segment_decoder_1_p1, bcd_to_7_segment_decoder_3_p1, bcd_to_7_segment_decoder_5_p1,
       bcd_to_7_segment_decoder_7_p1;
  wire [4:0] BTNC_out, register_1_q;
  wire [6:0] counter_2_q, multiplexer_3_out, multiplexer_4_out, register_2_q, register_3_q, register_4_q,
       register_5_q;

  Button BTNC (.out(BTNC_out[0]));
  Button BTNL (.out(BTNC_out[1]));
  Button BTNR (.out(BTNC_out[2]));
  Button BTNU (.out(BTNC_out[3]));
  Button BTND (.out(BTNC_out[4]));
  Clock clock_1 (.out(clock_1_out));
  Register #(.width(5)) register_1 (.D(BTNC_out), .en(1'b1), .clk(clock_1_out), .Q(register_1_q));  // open: clr
  xor xor_1 (xor_1_out, register_1_q[1], register_1_q[2]);
  not not_1 (not_1_out, register_1_q[1]);
  Counter #(.max('h3), .width(2)) counter_1 (
    .up(multiplexer_1_out), .count(xor_1_out), .clk(clock_1_out), .Q(counter_1_q));  // open: clr, load, D, carry
  Multiplexer multiplexer_1 (.in0(1'b0), .in1(1'b1), .out(multiplexer_1_out), .sel(not_1_out));
  xor xor_2 (xor_2_out, register_1_q[4], register_1_q[3]);
  D_Flip_Flop d_ff_1 (.D(xor_1_out), .clk(clock_1_out), .Q(d_ff_1_q));  // open: Qn, preset, reset
  Multiplexer multiplexer_2 (.in0(1'b1), .in1(1'b0), .out(multiplexer_2_out), .sel(register_1_q[4]));
  Register #(.width(7)) register_2 (
    .D(multiplexer_4_out), .en(decoder_1_out0), .clk(clock_1_out), .Q(register_2_q), .clr(in_1));
  Decoder #(.enable("false"), .select(2)) decoder_1 (
    .out0(decoder_1_out0), .out1(decoder_1_out1), .out2(decoder_1_out2), .out3(decoder_1_out3),
    .sel(counter_1_q));
  Register #(.width(7)) register_3 (
    .D(multiplexer_4_out), .en(decoder_1_out1), .clk(clock_1_out), .Q(register_3_q), .clr(in_1));
  Multiplexer #(.select(2), .width(7)) multiplexer_3 (
    .in0(register_2_q), .in1(register_3_q), .in2(register_4_q), .in3(register_5_q), .out(multiplexer_3_out),
    .sel(counter_1_q));
  Register #(.width(7)) register_4 (
    .D(multiplexer_4_out), .en(decoder_1_out2), .clk(clock_1_out), .Q(register_4_q), .clr(in_1));
  // Probe on multiplexer_3_out
  Counter #(.max('h7f), .width(7)) counter_2 (
    .clr(in_2), .load(d_ff_1_q), .up(multiplexer_2_out), .count(xor_2_out), .clk(clock_1_out),
    .D(multiplexer_3_out), .Q(counter_2_q));  // open: carry
  Register #(.width(7)) register_5 (
    .D(multiplexer_4_out), .en(decoder_1_out3), .clk(clock_1_out), .Q(register_5_q), .clr(in_1));
  Multiplexer #(.width(7)) multiplexer_4 (
    .in0(counter_2_q), .in1(multiplexer_3_out), .out(multiplexer_4_out), .sel(d_ff_1_q));
  _7_Segment_Display u_7_segment_display_1 ();  // open: g, f, a, b, e, d, c, dp
  // BCD_to_7_Segment_decoder bcd_to_7_segment_decoder_1: pin names not known; wires that end beside it: bcd_to_7_segment_decoder_1_p1
  assign bcd_to_7_segment_decoder_1_p1 = {{1{1'b0}}, register_2_q[6:4]};  // Bit_Extender bit_extender_1
  _7_Segment_Display u_7_segment_display_2 ();  // open: g, f, a, b, e, d, c, dp
  // BCD_to_7_Segment_decoder bcd_to_7_segment_decoder_2: pin names not known; wires that end beside it: register_2_q[3:0]
  _7_Segment_Display u_7_segment_display_3 ();  // open: g, f, a, b, e, d, c, dp
  // BCD_to_7_Segment_decoder bcd_to_7_segment_decoder_3: pin names not known; wires that end beside it: bcd_to_7_segment_decoder_3_p1
  assign bcd_to_7_segment_decoder_3_p1 = {{1{1'b0}}, register_3_q[6:4]};  // Bit_Extender bit_extender_2
  _7_Segment_Display u_7_segment_display_4 ();  // open: g, f, a, b, e, d, c, dp
  // BCD_to_7_Segment_decoder bcd_to_7_segment_decoder_4: pin names not known; wires that end beside it: register_3_q[3:0]
  _7_Segment_Display u_7_segment_display_5 ();  // open: g, f, a, b, e, d, c, dp
  // BCD_to_7_Segment_decoder bcd_to_7_segment_decoder_5: pin names not known; wires that end beside it: bcd_to_7_segment_decoder_5_p1
  assign bcd_to_7_segment_decoder_5_p1 = {{1{1'b0}}, register_4_q[6:4]};  // Bit_Extender bit_extender_3
  _7_Segment_Display u_7_segment_display_6 ();  // open: g, f, a, b, e, d, c, dp
  // BCD_to_7_Segment_decoder bcd_to_7_segment_decoder_6: pin names not known; wires that end beside it: register_4_q[3:0]
  _7_Segment_Display u_7_segment_display_7 ();  // open: g, f, a, b, e, d, c, dp
  // BCD_to_7_Segment_decoder bcd_to_7_segment_decoder_7: pin names not known; wires that end beside it: bcd_to_7_segment_decoder_7_p1
  _7_Segment_Display u_7_segment_display_8 ();  // open: g, f, a, b, e, d, c, dp
  // BCD_to_7_Segment_decoder bcd_to_7_segment_decoder_8: pin names not known; wires that end beside it: register_5_q[3:0]
  assign bcd_to_7_segment_decoder_7_p1 = {{1{1'b0}}, register_5_q[6:4]};  // Bit_Extender bit_extender_4

  // Notes on the sheet:
  //   TimeMin
  //   TimeHour
  //   AlarmMin
  //   AlarmHours
  //   The counter needs to get the value in the current register before loading anythign new but what's happening is that is't loading first
endmodule
