// Logisim project CUDP.circ as structural Verilog: 1 circuit, main circuit main
module main (
  input  [5:0] in_1,
  input  [3:0] in_2,
  input  [3:0] in_3,
  input  [2:0] in_4,
  input  [2:0] in_5,
  input  [4:0] in_6,
  input  [4:0] ConstantOne,
  input  [4:0] ConstantZero,
  input  [4:0] in_9,
  input  in_10
);

  wire AlarmSound_q, and_1_out, and_2_out, and_3_out, and_4_out, and_5_out, and_6_out, and_7_out, and_8_out,
       and_9_out, and_10_out, and_11_out, and_12_out, and_13_out, and_15_out, and_16_out, and_17_out,
       and_18_out, and_19_out, and_20_out, and_21_out, and_22_out, and_23_out, and_24_out, and_25_out,
       and_26_out, and_27_out, and_28_out, and_29_out, and_30_out, and_31_out, and_32_out, and_33_out,
       and_34_out, and_35_out, and_36_out, and_37_out, and_38_out, and_39_out, and_40_out, and_41_out,
       and_42_out, and_43_out, clock_1_out, d_ff_1_q, d_ff_2_q, j_k_ff_1_q, j_k_ff_1_qn, multiplexer_8_out,
       multiplexer_9_out, multiplexer_10_out, multiplexer_12_out, nand_1_out, nand_2_out, nor_1_out,
       nor_2_out, nor_3_out, nor_4_out, nor_5_out, not_1_out, not_2_out, not_3_out, not_4_out, not_5_out,
       not_6_out, not_7_out, not_8_out, not_9_out, not_10_out, not_11_out, not_12_out, not_13_out,
       not_14_out, not_15_out, not_16_out, not_18_out, or_1_out, or_2_out, or_3_out, or_4_out, or_5_out,
       or_6_out, or_8_out, or_9_out, or_11_out, or_12_out, or_13_out, or_14_out, or_15_out, or_16_out,
       State0_q, state1_q, xor_1_out, xor_2_out, ZFlag_out;
  wire [0:0] BL_q;
  wire [1:0] c1counter_q, or_10_out, subtractor_4_out, subtractor_5_out, subtractor_6_out, subtractor_7_out;
  wire [2:0] CurrentTimeHourTen_q, CurrentTimeMin_q_2, CurrentTimeMinTen_q, multiplexer_2_out,
       multiplexer_6_out;
  wire [3:0] bcd_to_7_segment_decoder_1_p1, bcd_to_7_segment_decoder_2_p1, bcd_to_7_segment_decoder_3_p1,
       CurrentTimeHour_q_2, CurrentTimeMin_q, CurrentTimeMinOne_q, multiplexer_1_out, multiplexer_4_out;
  wire [4:0] buttonState_q, LEDstate_q, multiplexer_7_out, subtractor_2_out, subtractor_3_out;
  wire [5:0] counter_1_q;
  wire [6:0] counter_2_q, multiplexer_3_out, multiplexer_5_out, multiplexer_11_out;
  wire [13:0] SetAlarmMin_q, subtractor_1_out;
  wire [13:11] CurrentTimeHour_q;

  Clock clock_1 (.out(clock_1_out));
  Counter #(.max('h3f), .width(6)) counter_1 (
    .load(and_1_out), .count(1'b1), .clk(clock_1_out), .D(in_1), .Q(counter_1_q));  // open: clr, up, carry
  Multiplexer #(.width(4)) multiplexer_1 (.in0(in_3), .in1(CurrentTimeMin_q), .out(multiplexer_1_out), .sel(or_1_out));
  or or_1 (or_1_out, state1_q, State0_q);
  and and_1 (and_1_out, counter_1_q[4], counter_1_q[3], counter_1_q[2], counter_1_q[1]);
  not not_1 (not_1_out, buttonState_q[3]);
  and and_2 (and_2_out, and_3_out, not_1_out);
  or or_2 (or_2_out, and_2_out, and_7_out);
  or or_3 (or_3_out, and_6_out, and_5_out, and_34_out, and_43_out);
  not not_2 (not_2_out, and_39_out);
  and and_3 (and_3_out, d_ff_2_q, not_2_out);
  D_Flip_Flop d_ff_1 (.D(or_2_out), .clk(clock_1_out), .Q(d_ff_1_q));  // open: Qn, preset, reset
  or or_4 (or_4_out, and_15_out, and_8_out);
  Counter #(.max('hf), .width(4)) CurrentTimeMinOne (
    .load(or_4_out), .count(1'b1), .clk(and_1_out), .D(multiplexer_1_out), .Q(CurrentTimeMinOne_q));  // open: clr, up, carry
  D_Flip_Flop d_ff_2 (.D(or_3_out), .clk(clock_1_out), .Q(d_ff_2_q));  // open: Qn, preset, reset
  and and_4 (and_4_out, buttonState_q[3], and_3_out);
  not not_3 (not_3_out, nor_1_out);
  and and_5 (and_5_out, d_ff_1_q, not_3_out);
  and and_6 (and_6_out, and_39_out, d_ff_2_q);
  and and_7 (and_7_out, nor_1_out, d_ff_1_q);
  _7_Segment_Display u_7_segment_display_1 ();  // open: g, f, a, b, e, d, c, dp
  // BCD_to_7_Segment_decoder bcd_to_7_segment_decoder_1: pin names not known; wires that end beside it: bcd_to_7_segment_decoder_1_p1
  and and_8 (and_8_out, CurrentTimeMinOne_q[3], CurrentTimeMinOne_q[0]);
  assign bcd_to_7_segment_decoder_1_p1 = {{1{1'b0}}, CurrentTimeHourTen_q};  // Bit_Extender bit_extender_1
  _7_Segment_Display u_7_segment_display_2 ();  // open: g, f, a, b, e, d, c, dp
  // BCD_to_7_Segment_decoder bcd_to_7_segment_decoder_2: pin names not known; wires that end beside it: bcd_to_7_segment_decoder_2_p1
  or or_5 (or_5_out, and_15_out, and_9_out);
  _7_Segment_Display u_7_segment_display_3 ();  // open: g, f, a, b, e, d, c, dp
  // BCD_to_7_Segment_decoder bcd_to_7_segment_decoder_3: pin names not known; wires that end beside it: bcd_to_7_segment_decoder_3_p1
  Multiplexer #(.width(3)) multiplexer_2 (.in0(in_4), .in1(CurrentTimeMin_q_2), .out(multiplexer_2_out), .sel(1'b0));
  // Probe on and_4_out
  assign bcd_to_7_segment_decoder_3_p1 = {{1{1'b0}}, CurrentTimeMinTen_q};  // Bit_Extender bit_extender_2
  Counter #(.max('h7), .width(3)) CurrentTimeMinTen (
    .load(or_5_out), .count(and_8_out), .clk(and_1_out), .D(multiplexer_2_out), .Q(CurrentTimeMinTen_q));  // open: clr, up, carry
  _7_Segment_Display u_7_segment_display_4 ();  // open: g, f, a, b, e, d, c, dp
  // BCD_to_7_Segment_decoder bcd_to_7_segment_decoder_4: pin names not known; wires that end beside it: CurrentTimeMinOne_q
  Multiplexer #(.width(7)) multiplexer_3 (
    .in0({CurrentTimeMinTen_q, CurrentTimeMinOne_q}), .in1(counter_2_q), .out(multiplexer_3_out),
    .sel(or_6_out));
  or or_6 (or_6_out, state1_q, State0_q);
  or or_7 (or_10_out[1], and_6_out, and_5_out);
  or or_8 (or_8_out, and_15_out, and_10_out);
  Multiplexer #(.width(4)) multiplexer_4 (.in0(in_2), .in1(CurrentTimeHour_q_2), .out(multiplexer_4_out), .sel(1'b0));
  and and_9 (and_9_out, CurrentTimeMinTen_q[2], and_8_out, CurrentTimeMinTen_q[0]);
  Register #(.width(7)) CurrentTimeMin (
    .D(multiplexer_3_out), .en(nand_1_out), .clk(clock_1_out), .Q({CurrentTimeMin_q_2, CurrentTimeMin_q}));  // open: clr
  Counter #(.max('hf), .width(4)) CurrentTimeHourOne (
    .load(or_8_out), .count(and_9_out), .clk(and_1_out), .D(multiplexer_4_out),
    .Q(bcd_to_7_segment_decoder_2_p1));  // open: clr, up, carry
  J_K_Flip_Flop j_k_ff_1 (
    .J(c1counter_q[0]), .K(c1counter_q[1]), .Q(j_k_ff_1_q), .Qn(j_k_ff_1_qn));  // open: clk, preset, reset
  Multiplexer #(.width(7)) multiplexer_5 (
    .in0({CurrentTimeHourTen_q, bcd_to_7_segment_decoder_2_p1}), .in1(counter_2_q), .out(multiplexer_5_out),
    .sel(or_9_out));
  or or_9 (or_9_out, state1_q, State0_q);
  or or_10 (or_10_out[0], and_2_out, and_7_out);
  and and_10 (and_10_out, bcd_to_7_segment_decoder_2_p1[3], bcd_to_7_segment_decoder_2_p1[0], and_9_out);
  Register #(.width(7)) CurrentTimeHour (
    .D(multiplexer_5_out), .en(j_k_ff_1_q), .clk(clock_1_out), .Q({CurrentTimeHour_q, CurrentTimeHour_q_2}));  // open: clr
  T_Flip_Flop BL (.T(1'b1), .clk(clock_1_out), .Q(BL_q[0]));  // open: Qn, reset, preset
  or or_11 (or_11_out, and_15_out, and_19_out);
  not not_4 (not_4_out, nor_4_out);
  and and_11 (and_11_out, and_28_out, not_4_out);
  not not_5 (not_5_out, nor_4_out);
  and and_12 (and_12_out, or_12_out, not_5_out);
  not not_6 (not_6_out, nor_5_out);
  and and_13 (and_13_out, and_12_out, not_6_out);
  Counter #(.max('h7), .width(3)) CurrentTimeHourTen (
    .load(or_11_out), .count(and_10_out), .clk(and_1_out), .D(multiplexer_6_out), .Q(CurrentTimeHourTen_q));  // open: clr, up, carry
  Subtractor #(.width(14)) subtractor_1 (
    .a(SetAlarmMin_q), .b({CurrentTimeHour_q, CurrentTimeHour_q_2, CurrentTimeMin_q_2, CurrentTimeMin_q}),
    .out(subtractor_1_out));  // open: bin, bout
  or or_12 (or_12_out, and_28_out, and_29_out);
  Multiplexer #(.width(3)) multiplexer_6 (.in0(in_5), .in1(CurrentTimeHour_q), .out(multiplexer_6_out), .sel(1'b0));
  Register #(.width(7)) SetAlarmMin (
    .D(counter_2_q), .en(j_k_ff_1_qn), .clk(clock_1_out), .Q(SetAlarmMin_q[6:0]));  // open: clr
  Multiplexer #(.select(2), .width(5)) multiplexer_7 (
    .in0(LEDstate_q), .in1({4'b0000, BL_q[0]}), .in2(in_9), .out(multiplexer_7_out));  // open: in3, sel
  Multiplexer #(.select(2)) multiplexer_8 (
    .in0(AlarmSound_q), .in1(1'b1), .in2(in_10), .out(multiplexer_8_out), .sel(or_10_out));  // open: in3
  // AND_Gate and_14 has open pins: in0=nor_4_out, in1=and_28_out, out=open
  and and_15 (and_15_out, CurrentTimeHourTen_q[1], and_20_out, and_21_out, and_16_out);
  and and_16 (and_16_out, bcd_to_7_segment_decoder_2_p1[0], bcd_to_7_segment_decoder_2_p1[1]);
  Counter #(.max('h7f), .width(7)) counter_2 (
    .load(xor_2_out), .up(multiplexer_10_out), .count(xor_1_out), .clk(clock_1_out), .D(multiplexer_11_out),
    .Q(counter_2_q));  // open: clr, carry
  and and_17 (and_17_out, nor_4_out, or_12_out);
  and and_18 (and_18_out, nor_5_out, and_12_out);
  and and_19 (and_19_out, CurrentTimeHourTen_q[1], and_10_out);
  nand nand_1 (nand_1_out, c1counter_q[0], c1counter_q[1]);
  or or_13 (or_13_out, or_10_out[0], or_10_out[1]);
  or or_14 (or_14_out, and_4_out, and_27_out);
  and and_20 (and_20_out, CurrentTimeMinTen_q[2], CurrentTimeMinTen_q[0]);
  Register #(.width(7)) SetAlarmHour (
    .D(counter_2_q), .en(and_22_out), .clk(clock_1_out), .Q(SetAlarmMin_q[13:7]));  // open: clr
  Register #(.width(5)) LEDstate (
    .D(multiplexer_7_out), .en(or_13_out), .clk(clock_1_out), .Q(LEDstate_q));  // open: clr
  nor ZFlag (ZFlag_out, subtractor_1_out[13], subtractor_1_out[12], subtractor_1_out[11], subtractor_1_out[10], subtractor_1_out[9], subtractor_1_out[8], subtractor_1_out[7], subtractor_1_out[6], subtractor_1_out[5], subtractor_1_out[4], subtractor_1_out[3], subtractor_1_out[2], subtractor_1_out[1], subtractor_1_out[0]);
  D_Flip_Flop State0 (.D(or_14_out), .clk(clock_1_out), .Q(State0_q));  // open: Qn, preset, reset
  and and_21 (and_21_out, CurrentTimeMinOne_q[0], CurrentTimeMinOne_q[3]);
  Register #(.width(5)) buttonState (.D(in_6), .clk(clock_1_out), .Q(buttonState_q));  // open: en, clr
  and and_22 (and_22_out, c1counter_q[1], c1counter_q[1]);
  Multiplexer multiplexer_9 (.in0(AlarmSound_q), .in1(multiplexer_8_out), .out(multiplexer_9_out), .sel(or_13_out));
  and and_23 (and_23_out, and_33_out, not_8_out);
  and and_24 (and_24_out, and_23_out, not_9_out);
  and and_25 (and_25_out, and_24_out, not_10_out);
  Multiplexer multiplexer_10 (.in0(1'b1), .in1(1'b0), .out(multiplexer_10_out), .sel(buttonState_q[4]));
  Subtractor #(.width(5)) subtractor_2 (.a(buttonState_q), .b(ConstantOne), .out(subtractor_2_out));  // open: bin, bout
  Subtractor #(.width(5)) subtractor_3 (
    .a(buttonState_q), .b(ConstantZero), .out(subtractor_3_out));  // open: bin, bout
  D_Flip_Flop AlarmSound (.D(multiplexer_9_out), .clk(clock_1_out), .Q(AlarmSound_q));  // open: Qn, preset, reset
  not not_7 (not_7_out, nor_2_out);
  and and_26 (and_26_out, State0_q, not_7_out);
  not not_8 (not_8_out, nand_2_out);
  not not_9 (not_9_out, buttonState_q[3]);
  not not_10 (not_10_out, buttonState_q[4]);
  not not_11 (not_11_out, and_4_out);
  and and_27 (and_27_out, and_25_out, not_11_out);
  not not_12 (not_12_out, nor_3_out);
  and and_28 (and_28_out, and_26_out, not_12_out);
  and and_29 (and_29_out, state1_q, not_13_out);
  and and_30 (and_30_out, and_40_out, not_14_out);
  and and_31 (and_31_out, and_30_out, not_15_out);
  not not_13 (not_13_out, nand_2_out);
  not not_14 (not_14_out, buttonState_q[3]);
  not not_15 (not_15_out, buttonState_q[4]);
  not not_16 (not_16_out, buttonState_q[3]);
  and and_32 (and_32_out, and_31_out, not_16_out);
  Multiplexer #(.select(2), .width(7)) multiplexer_11 (
    .in0({CurrentTimeMin_q_2, CurrentTimeMin_q}), .in1({CurrentTimeHour_q, CurrentTimeHour_q_2}),
    .in2(SetAlarmMin_q[6:0]), .in3(SetAlarmMin_q[13:7]), .out(multiplexer_11_out), .sel(c1counter_q));
  or or_15 (or_15_out, subtractor_2_out[0], subtractor_2_out[1], subtractor_2_out[2], subtractor_2_out[3], subtractor_2_out[4]);
  nor nor_1 (nor_1_out, subtractor_3_out[0], subtractor_3_out[1], subtractor_3_out[2], subtractor_3_out[3], subtractor_3_out[4]);
  and and_33 (and_33_out, nor_2_out, State0_q);
  and and_34 (and_34_out, nand_2_out, and_33_out);
  and and_35 (and_35_out, buttonState_q[3], and_23_out);
  and and_36 (and_36_out, buttonState_q[4], and_24_out);
  and and_37 (and_37_out, and_4_out, and_25_out);
  and and_38 (and_38_out, nor_3_out, and_26_out);
  not not_17 (buttonState_q[3], or_15_out);
  and and_39 (and_39_out, or_15_out, ZFlag_out);
  D_Flip_Flop state1 (.D(or_16_out), .clk(clock_1_out), .Q(state1_q));  // open: Qn, preset, reset
  or or_16 (or_16_out, and_38_out, and_32_out, and_13_out);
  and and_40 (and_40_out, nand_2_out, state1_q);
  and and_41 (and_41_out, buttonState_q[3], and_40_out);
  and and_42 (and_42_out, buttonState_q[4], and_30_out);
  and and_43 (and_43_out, buttonState_q[3], and_31_out);
  nand nand_2 (nand_2_out, buttonState_q[0], buttonState_q[4]);
  xor xor_1 (xor_1_out, buttonState_q[4], buttonState_q[3]);
  not not_18 (not_18_out, buttonState_q[1]);
  Multiplexer multiplexer_12 (.in0(1'b0), .in1(1'b1), .out(multiplexer_12_out), .sel(not_18_out));
  xor xor_2 (xor_2_out, buttonState_q[2], buttonState_q[1]);
  Counter #(.max('h3), .width(2)) c1counter (
    .up(multiplexer_12_out), .count(xor_2_out), .clk(clock_1_out), .Q(c1counter_q));  // open: clr, load, D, carry
  Subtractor #(.width(2)) subtractor_4 (.a(c1counter_q), .b(2'b10), .out(subtractor_4_out));  // open: bin, bout
  Subtractor #(.width(2)) subtractor_5 (.a(c1counter_q), .b(2'b11), .out(subtractor_5_out));  // open: bin, bout
  Subtractor #(.width(2)) subtractor_6 (.a(c1counter_q), .b(2'b00), .out(subtractor_6_out));  // open: bin, bout
  Subtractor #(.width(2)) subtractor_7 (.a(c1counter_q), .b(2'b01), .out(subtractor_7_out));  // open: bin, bout
  nor nor_2 (nor_2_out, subtractor_6_out[0], subtractor_6_out[1]);
  nor nor_3 (nor_3_out, subtractor_7_out[0], subtractor_7_out[1]);
  nor nor_4 (nor_4_out, subtractor_4_out[0], subtractor_4_out[1]);
  nor nor_5 (nor_5_out, subtractor_5_out[0], subtractor_5_out[1]);

  // Notes on the sheet:
  //   ConstantOne: initial=0x1
  //   clock
  //   clock
  //   LEDstate <- 00000
  //   AlarmSound = 0
  //   or gate
  //   LEDstate <-BL
  //   AlarmSound <- 1
  //   NOT(Zflag ==0 & buttonState != 00001)
  //   buttonState == 00001
  //   IF2
  //   Clock State
  //   Zflag == 0 & buttonState != 00001
  //   IF1
  //   buttonState == 00000
  //   AlarmSound = 1
  //   LEDstate <- BL
  //   1 adjust 0 clockalarm 
  //   or gates of the states
  //   TimeMin
  //   problem to be solved
  //   enable for timemine register
  //   TimeHour
  //   EN AlMin
  //   00 no load
  //   01 BL load
  //   10 ZeroLoad
  //   LEDstate = 00001
  //   ZFlag Subtractor
  //   c1 == 2
  //   c1 == 2
  //   c1 == 3
  //   LEDstate MUX
  //   AlarmSound MUX
  //   EN Alhour
  //   c1==0 and buttonState != (10000 | 01000 | 00001) 
  //   buttonState != 00001
  //   buttonState == 0
  //   buttonState != (10000 | 01000 | 00001
  //   buttonState == 01000
  //   buttonState == 10000
  //   buttonState == 00001
  //   c1 == 1
  //   c1 counter bit 0
  //   c1 == 0
  //   buttonState != (10000 | 01000 | 00001
  //   buttonState == 01000
  //   buttonState == 10000
  //   buttonState == 00001
  //   c1 counter bit 1
  //   buttonState == 00001
  //   clock
  //   c1 == 2
  //   increment time hour
  //   decrement time hour
  //   increment time min
  //   decrement time min
  //   c1 == 1
  //   4
  //   3
  //   1
  //   2
  //   c1 == 0
  //   c1 == 1
  //   c1 == 2
  //   c1 == 3
endmodule
